# Fritzing sketch hee (saved by Fritzing 0.9.2b)
breadboards: 1

parts:
  IC1 = IC, DIP package, 14 pins [chip_label=16F1705]
  R1 = Trimmer Potentiometer [maximum_resistance=10kΩ package=THT]
  SPKR1 = Loudspeaker
  S1 = Pushbutton [package="[THT]"]
  VCC1 = Battery

nets:
  N1: IC1.pin1, VCC1.+
  N2: IC1.pin5, S1.Pin_1, S1.Pin_2
  N3: IC1.pin8, R1.leg1
  N4: IC1.pin14, SPKR1.pin1, S1.Pin_3, S1.Pin_4, VCC1.-
  N5: R1.wiper, SPKR1.pin2
